# Fritzing sketch Tinyg_DM542T_2Driver (saved by Fritzing 0.9.3b)
circuit board: 11.8cm x 8cm
breadboards: 1

parts:
  C1 = Electrolytic Capacitor [capacitance=1µF voltage=63V package="100 mil [THT, electrolytic]"]
  R2 = Resistor [tolerance=±5% resistance=4.7k package=THT]
  R1 = Resistor [tolerance=±5% resistance=4.7k package=THT]
  R3 = Resistor [tolerance=±5% resistance=4.7k package=THT]
  Q1 = NPN-Transistor [package="TO92 [THT]"]
  Q2 = NPN-Transistor [package="TO92 [THT]"]
  Q3 = NPN-Transistor [package="TO92 [THT]"]
  j11 = Crimp terminal - 2 pins [part_number=804-102 package=THT]
  J10 = Crimp terminal - 2 pins [part_number=804-102 package=THT]
  J12 = Crimp terminal - 2 pins [part_number=804-102 package=THT]
  R24_3 = Resistor [tolerance=±5% resistance=2.2k package=THT]
  R24_5 = Resistor [tolerance=±5% resistance=2.2k package=THT]
  J22 = Crimp terminal - 2 pins [part_number=804-102 package=THT]
  R12_2 = Resistor [tolerance=±5% resistance=1k package=THT]
  R24_6 = Resistor [tolerance=±5% resistance=2.2k package=THT]
  J24_3 = Crimp terminal - 2 pins [part_number=804-102 package=THT]
  J24_1 = Crimp terminal - 2 pins [part_number=804-102 package=THT]
  J24_2 = Crimp terminal - 2 pins [part_number=804-102 package=THT]
  J20 = Crimp terminal - 2 pins [part_number=804-102 package=THT]
  R24_2 = Resistor [tolerance=±5% resistance=2.2k package=THT]
  U10 = mystery part, 3 pins [chip_label=?]
  R12_3 = Resistor [tolerance=±5% resistance=1k package=THT]
  U11 = mystery part, 3 pins [chip_label=?]
  R24_4 = Resistor [tolerance=±5% resistance=2.2k package=THT]
  U21 = mystery part, 3 pins [chip_label=?]
  R12_5 = Resistor [tolerance=±5% resistance=1k package=THT]
  U12 = mystery part, 3 pins [chip_label=?]
  R12_6 = Resistor [tolerance=±5% resistance=1k package=THT]
  U20 = mystery part, 3 pins [chip_label=?]
  U22 = mystery part, 3 pins [chip_label=?]
  J12_2 = Crimp terminal - 2 pins [part_number=804-102 package=THT]
  J24_4 = Crimp terminal - 2 pins [part_number=804-102 package=THT]
  U12/24 = mystery part, 3 pins [chip_label=?]
  V1 = DC Power [voltage=12V]
  V2 = DC Power [voltage=24V]
  JTinyg = Screw terminal - 5 pins [part_number=804-105 package=THT]
  C2 = Electrolytic Capacitor [capacitance=1µF voltage=63V package="100 mil [THT, electrolytic]"]
  R12_4 = Resistor [tolerance=±5% resistance=1k package=THT]
  j12 = Crimp terminal - 2 pins [part_number=804-102 package=THT]
  R24_1 = Resistor [tolerance=±5% resistance=2.2k package=THT]
  R12_1 = Resistor [tolerance=±5% resistance=1k package=THT]

nets:
  GND: C1.-, R2.Pin_1, R1.Pin_1, R3.Pin_1, Q1.S, Q2.S, Q3.S, J24_3.pin1, J24_1.pin1, J24_2.pin1, J12_2.pin_2, J24_4.pin1, V1.V-, V2.V-, JTinyg.pin_2, C2.-
  N1: C1.+, J12_2.pin1, U12/24.pin1, V1.V+, JTinyg.pin1
  N2: R2.Pin_0, Q2.G, JTinyg.pin_4
  N3: R1.Pin_0, Q1.G, JTinyg.pin_3
  N4: R3.Pin_0, Q3.G, JTinyg.pin_5
  N5: Q1.D, J10.pin1, J20.pin1
  N6: Q2.D, j11.pin1, j12.pin1
  N7: Q3.D, J12.pin1, J22.pin1
  N8: j11.pin_2, R24_3.Pin_0, R12_3.Pin_0
  N9: J10.pin_2, R24_1.Pin_0, R12_1.Pin_0
  N10: J12.pin_2, R24_5.Pin_0, R12_5.Pin_0
  N11: R24_3.Pin_1, U11.pin1
  N12: R24_5.Pin_1, U12.pin1
  N13: J22.pin_2, R24_6.Pin_1, R12_6.Pin_1
  N14: R12_2.Pin_0, U20.pin3
  N15: R12_2.Pin_1, J20.pin_2, R24_2.Pin_1
  N16: R24_6.Pin_0, U22.pin1
  N17: J24_3.pin_2, J24_1.pin_2, J24_2.pin_2, J24_4.pin_2, U12/24.pin3, V2.V+, C2.+
  N18: R24_2.Pin_0, U20.pin1
  N19: U10.pin1, R24_1.Pin_1
  N20: U10.pin2, U11.pin2, U21.pin2, U12.pin2, U20.pin2, U22.pin2, U12/24.pin2
  N21: U10.pin3, R12_1.Pin_1
  N22: R12_3.Pin_1, U11.pin3
  N23: R24_4.Pin_0, R12_4.Pin_1, j12.pin_2
  N24: R24_4.Pin_1, U21.pin1
  N25: U21.pin3, R12_4.Pin_0
  N26: R12_5.Pin_1, U12.pin3
  N27: R12_6.Pin_0, U22.pin3

notes:
  12V
  Wago 804-105
  GND
  Step
  Dir
  Ena
  24V
  Wago 804-102
  Dir-
  Dir+
  Ena+
  Ena-
  Pul-
  Pul+
  Chanl 1
  Chanl 2
  R12.n = 1kOhm
  R24.n = 2kOhm
  R1..3 = 5kOhm
  Q1..3 = FET 2N7000
  C1..2 = 1mF 63V
  JTinyG=Connect2JtinyG
  J1n=DM542T Driver1
  J2n=DM542T Driver2
  TinyG for 2  DM542T Driver
  U1n.0.U2n= Jumper
  by Francis Hartmann
  20180923 rev. 1

custom parts:
  NPN-Transistor: A standard NPN-transistor
  Crimp terminal - 2 pins: Wago Crimp terminal with 2 pins 5mm spacing
  Screw terminal - 5 pins: Wago Crimp terminal with 5 pins 5mm spacing
